# Fritzing sketch Basic_Keypad_Usage (saved by Fritzing 0.9.0b)
breadboards: 1

parts:
  Matrix_Keypad = KEYPAD 4x4
  Arduino_Micro = Arduino Micro (Rev3) [part_number="MCU 1"]

nets:
  N1: Matrix_Keypad.col1, Arduino_Micro.D11_PWM
  N2: Matrix_Keypad.col2, Arduino_Micro.D10_PWM/A10
  N3: Matrix_Keypad.col3, Arduino_Micro.D9_PWM/A9
  N4: Matrix_Keypad.col4, Arduino_Micro.D8_PWM/A8
  N5: Matrix_Keypad.row1, Arduino_Micro.D7
  N6: Matrix_Keypad.row2, Arduino_Micro.D6_PWM/A7
  N7: Matrix_Keypad.row3, Arduino_Micro.D5_PWM
  N8: Matrix_Keypad.row4, Arduino_Micro.D4_PWM/A6

custom parts:
  KEYPAD 4x4: Matrix keypad 16 buttons, 4 rows x 4 columns
