# Fritzing sketch Basic Ultrasonic Distance Measurement (saved by Fritzing 0.9.0b)
breadboards: 1

parts:
  MCU1 = Arduino Micro (Rev3)
  SENSOR1 = SRF05 Ultrasonic Rangefinder

nets:
  N1: MCU1.D12_PWM/A11, SENSOR1.Echo
  GND: MCU1.GND, SENSOR1.GND
  5V: MCU1.5V, SENSOR1.VCC
  N2: MCU1.D13_PWM, SENSOR1.Trig
